// Logisim project segemnt b.circ as structural Verilog: 1 circuit, main circuit main
module main (
  input  x,
  input  y,
  input  z,
  input  t,
  output b
);

  wire not_1_out, not_2_out, not_3_out, not_4_out, x_y__out, x_z_t__out, x_zt_out, xz_t_out, xzt__out,
       z_y__out;

  not not_1 (not_1_out, x);
  not not_2 (not_2_out, y);
  not not_3 (not_3_out, z);
  not not_4 (not_4_out, t);
  and x_y_ (x_y__out, not_1_out, not_2_out);
  and x_z_t_ (x_z_t__out, not_1_out, not_3_out, not_4_out);
  and x_zt (x_zt_out, not_1_out, z, t);
  and z_y_ (z_y__out, not_3_out, not_2_out);
  and xz_t (xz_t_out, x, not_3_out, t);
  and xzt_ (xzt__out, x, z, not_4_out);
  or or_1 (b, x_y__out, x_z_t__out, x_zt_out, z_y__out, xz_t_out, xzt__out);
endmodule
