// Logisim project Afficheur 7 segments.circ as structural Verilog: 1 circuit, main circuit main
module main (
  input  x,
  input  y,
  input  z,
  input  t,
  output a,
  output b,
  output c,
  output d,
  output e,
  output f,
  output g
);

  Segment_a_main u_a (.x(x), .y(y), .z(z), .t(t), .a(a));
  Segment_b_main u_b (.x(x), .y(y), .z(z), .t(t), .b(b));
  Segment_c_main u_c (.x(x), .y(y), .z(z), .t(t), .c(c));
  Segment_d_main u_d (.x(x), .y(y), .z(z), .t(t), .d(d));
  Segment_e_main u_e (.x(x), .y(y), .z(z), .t(t), .e(e));
  Segment_f_main u_f (.x(x), .y(y), .z(z), .t(t), .f(f));
  Segment_g_main u_g (.x(x), .y(y), .z(z), .t(t), .g(g));
  _7_Segment_Display u_7_segment_display_1 (.g(g), .f(f), .a(a), .b(b), .e(e), .d(d), .c(c), .dp(1'b0));
endmodule
