// Logisim project Segment_a.circ as structural Verilog: 1 circuit, main circuit main
module main (
  input  x,
  input  y,
  input  z,
  input  t,
  output a
);

  wire and_1_out, and_2_out, not_1_out, not_2_out, not_3_out, not_4_out;

  not not_1 (not_1_out, x);
  not not_2 (not_2_out, y);
  not not_3 (not_3_out, z);
  not not_4 (not_4_out, t);
  and and_1 (and_1_out, not_1_out, not_2_out, not_3_out, t);
  and and_2 (and_2_out, not_4_out, not_3_out, y, not_1_out);
  nor nor_1 (a, and_1_out, and_2_out);
endmodule
