// Logisim project Exercice 2.circ as structural Verilog: 1 circuit, main circuit main
module main (
  input  [1:0] in_1,
  output S0,
  output S1,
  output S3,
  output S2
);

  wire not_1_out, not_2_out;

  not not_1 (not_1_out, in_1[1]);
  not not_2 (not_2_out, in_1[0]);
  and and_1 (S0, not_1_out, not_2_out);
  and and_2 (S3, in_1[0], in_1[1]);
  and and_3 (S2, not_2_out, in_1[1]);
  and and_4 (S1, not_1_out, in_1[0]);
endmodule
