// Logisim project Exercice 3.2.circ as structural Verilog: 1 circuit, main circuit main
module main (
  input  in_1,
  input  in_2,
  input  in_3,
  output S,
  output R
);

  wire and_1_out, and_2_out, xor_1_out;

  and and_1 (and_1_out, in_1, in_2);
  xor xor_1 (xor_1_out, in_1, in_2);
  xor xor_2 (S, xor_1_out, in_3);
  and and_2 (and_2_out, in_3, xor_1_out);
  or or_1 (R, and_2_out, and_1_out);
endmodule
