// Logisim project Exercice 3.circ as structural Verilog: 1 circuit, main circuit main
module main (
  input  in_1,
  input  in_2,
  output S,
  output R
);

  xor xor_1 (S, in_1, in_2);
  and and_1 (R, in_1, in_2);
endmodule
