// Logisim project Afficheur 7 segements.circ as structural Verilog: 26 circuits, main circuit AFFICHEUR7SEGMENTS
module AFFICHEUR7SEGMENTS (
  input  [3:0] bin,
  output [7:0] out_2
);

  A A (.in_1(bin), .out_2(out_2[2]));
  B B (.in_1(bin), .out_2(out_2[3]));
  C C (.in_1(bin), .out_2(out_2[6]));
  D D (.in_1(bin), .out_2(out_2[5]));
  E E (.in_1(bin), .out_2(out_2[4]));
  F F (.in_1(bin), .out_2(out_2[1]));
  G G (.in_1(bin), .out_2(out_2[0]));
  _7_Segment_Display u_7_segment_display_1 (
    .g(out_2[0]), .f(out_2[1]), .a(out_2[2]), .b(out_2[3]), .e(out_2[4]), .d(out_2[5]), .c(out_2[6]),
    .dp(1'b0));

  assign out_2[7] = 1'b0;
endmodule

module A (
  input  [3:0] in_1,
  output out_2
);

  wire _0_out_2, _2_out_2, _3_out_2, _5_out_2, _6_out_2, _7_out_2, _8_out_2, _9_out_2, _10_out_2, _12_out_2,
       _14_out_2, _15_out_2;

  _2 _2 (.in_1(in_1), .out_2(_2_out_2));
  _3 _3 (.in_1(in_1), .out_2(_3_out_2));
  _5 _5 (.in_1(in_1), .out_2(_5_out_2));
  _6 _6 (.in_1(in_1), .out_2(_6_out_2));
  _7 _7 (.in_1(in_1), .out_2(_7_out_2));
  _8 _8 (.in_1(in_1), .out_2(_8_out_2));
  _9 _9 (.in_1(in_1), .out_2(_9_out_2));
  _10 _10 (.in_1(in_1), .out_2(_10_out_2));
  _12 _12 (.in_1(in_1), .out_2(_12_out_2));
  _14 _14 (.in_1(in_1), .out_2(_14_out_2));
  _15 _15 (.in_1(in_1), .out_2(_15_out_2));
  _0 _0 (.in_1(in_1), .out_2(_0_out_2));
  or A (out_2, _2_out_2, _3_out_2, _5_out_2, _6_out_2, _7_out_2, _8_out_2, _9_out_2, _10_out_2, _12_out_2, _14_out_2, _0_out_2, _15_out_2);
endmodule

module _1 (
  input  [3:0] in_1,
  output out_2
);

  wire not_1_out, not_2_out, not_3_out;

  not not_1 (not_1_out, in_1[3]);
  not not_2 (not_2_out, in_1[2]);
  not not_3 (not_3_out, in_1[1]);
  and and_1 (out_2, not_1_out, not_2_out, not_3_out, in_1[0]);
endmodule

module _2 (
  input  [3:0] in_1,
  output out_2
);

  wire not_1_out, not_2_out, not_3_out;

  not not_1 (not_1_out, in_1[3]);
  not not_2 (not_2_out, in_1[2]);
  not not_3 (not_3_out, in_1[0]);
  and and_1 (out_2, not_1_out, not_2_out, in_1[1], not_3_out);
endmodule

module _3 (
  input  [3:0] in_1,
  output out_2
);

  wire not_1_out, not_2_out;

  not not_1 (not_1_out, in_1[3]);
  not not_2 (not_2_out, in_1[2]);
  and and_1 (out_2, not_1_out, not_2_out, in_1[1], in_1[0]);
endmodule

module _4 (
  input  [3:0] in_1,
  output out_2
);

  wire not_1_out, not_2_out, not_3_out;

  not not_1 (not_1_out, in_1[3]);
  not not_2 (not_2_out, in_1[1]);
  not not_3 (not_3_out, in_1[0]);
  and and_1 (out_2, not_1_out, in_1[2], not_2_out, not_3_out);
endmodule

module _5 (
  input  [3:0] in_1,
  output out_2
);

  wire not_1_out, not_2_out;

  not not_1 (not_1_out, in_1[3]);
  not not_2 (not_2_out, in_1[1]);
  and and_1 (out_2, not_1_out, in_1[2], not_2_out, in_1[0]);
endmodule

module _6 (
  input  [3:0] in_1,
  output out_2
);

  wire not_1_out, not_2_out;

  not not_1 (not_1_out, in_1[3]);
  not not_2 (not_2_out, in_1[0]);
  and and_1 (out_2, not_1_out, in_1[2], in_1[1], not_2_out);
endmodule

module _7 (
  input  [3:0] in_1,
  output out_2
);

  wire not_1_out;

  not not_1 (not_1_out, in_1[3]);
  and and_1 (out_2, not_1_out, in_1[2], in_1[1], in_1[0]);
endmodule

module _8 (
  input  [3:0] in_1,
  output out_2
);

  wire not_1_out, not_2_out, not_3_out;

  not not_1 (not_1_out, in_1[2]);
  not not_2 (not_2_out, in_1[1]);
  not not_3 (not_3_out, in_1[0]);
  and and_1 (out_2, in_1[3], not_1_out, not_2_out, not_3_out);
endmodule

module _9 (
  input  [3:0] in_1,
  output out_2
);

  wire not_1_out, not_2_out;

  not not_1 (not_1_out, in_1[2]);
  not not_2 (not_2_out, in_1[1]);
  and and_1 (out_2, in_1[3], not_1_out, not_2_out, in_1[0]);
endmodule

module _10 (
  input  [3:0] in_1,
  output out_2
);

  wire not_1_out, not_2_out;

  not not_1 (not_1_out, in_1[2]);
  not not_2 (not_2_out, in_1[0]);
  and and_1 (out_2, in_1[3], not_1_out, in_1[1], not_2_out);
endmodule

module _11 (
  input  [3:0] in_1,
  output out_2
);

  wire not_1_out;

  not not_1 (not_1_out, in_1[2]);
  and and_1 (out_2, in_1[3], not_1_out, in_1[1], in_1[0]);
endmodule

module _12 (
  input  [3:0] in_1,
  output out_2
);

  wire not_1_out, not_2_out;

  not not_1 (not_1_out, in_1[1]);
  not not_2 (not_2_out, in_1[0]);
  and and_1 (out_2, in_1[3], in_1[2], not_1_out, not_2_out);
endmodule

module _13 (
  input  [3:0] in_1,
  output out_2
);

  wire not_1_out;

  not not_1 (not_1_out, in_1[1]);
  and and_1 (out_2, in_1[3], in_1[2], not_1_out, in_1[0]);
endmodule

module _14 (
  input  [3:0] in_1,
  output out_2
);

  wire not_1_out;

  not not_1 (not_1_out, in_1[0]);
  and and_1 (out_2, in_1[3], in_1[2], in_1[1], not_1_out);
endmodule

module _15 (
  input  [3:0] in_1,
  output out_2
);

  and and_1 (out_2, in_1[3], in_1[2], in_1[1], in_1[0]);
endmodule

module B (
  input  [3:0] in_1,
  output out_2
);

  wire _0_out_2, _1_out_2, _2_out_2, _3_out_2, _4_out_2, _7_out_2, _8_out_2, _9_out_2, _10_out_2, _13_out_2;

  _1 _1 (.in_1(in_1), .out_2(_1_out_2));
  _2 _2 (.in_1(in_1), .out_2(_2_out_2));
  _3 _3 (.in_1(in_1), .out_2(_3_out_2));
  _4 _4 (.in_1(in_1), .out_2(_4_out_2));
  _7 _7 (.in_1(in_1), .out_2(_7_out_2));
  _8 _8 (.in_1(in_1), .out_2(_8_out_2));
  _9 _9 (.in_1(in_1), .out_2(_9_out_2));
  _10 _10 (.in_1(in_1), .out_2(_10_out_2));
  _13 _13 (.in_1(in_1), .out_2(_13_out_2));
  _0 _0 (.in_1(in_1), .out_2(_0_out_2));
  or B (out_2, _1_out_2, _2_out_2, _3_out_2, _4_out_2, _7_out_2, _8_out_2, _9_out_2, _10_out_2, _13_out_2, _0_out_2);
endmodule

module C (
  input  [3:0] in_1,
  output out_2
);

  wire _0_out_2, _1_out_2, _3_out_2, _4_out_2, _5_out_2, _6_out_2, _7_out_2, _8_out_2, _9_out_2, _10_out_2,
       _11_out_2, _13_out_2;

  _1 _1 (.in_1(in_1), .out_2(_1_out_2));
  _3 _3 (.in_1(in_1), .out_2(_3_out_2));
  _4 _4 (.in_1(in_1), .out_2(_4_out_2));
  _5 _5 (.in_1(in_1), .out_2(_5_out_2));
  _6 _6 (.in_1(in_1), .out_2(_6_out_2));
  _7 _7 (.in_1(in_1), .out_2(_7_out_2));
  _8 _8 (.in_1(in_1), .out_2(_8_out_2));
  _9 _9 (.in_1(in_1), .out_2(_9_out_2));
  _10 _10 (.in_1(in_1), .out_2(_10_out_2));
  _11 _11 (.in_1(in_1), .out_2(_11_out_2));
  _13 _13 (.in_1(in_1), .out_2(_13_out_2));
  _0 _0 (.in_1(in_1), .out_2(_0_out_2));
  or C (out_2, _1_out_2, _3_out_2, _4_out_2, _5_out_2, _6_out_2, _7_out_2, _8_out_2, _9_out_2, _10_out_2, _11_out_2, _13_out_2, _0_out_2);
endmodule

module D (
  input  [3:0] in_1,
  output out_2
);

  wire _0_out_2, _2_out_2, _3_out_2, _5_out_2, _6_out_2, _8_out_2, _9_out_2, _11_out_2, _12_out_2, _13_out_2,
       _14_out_2;

  _2 _2 (.in_1(in_1), .out_2(_2_out_2));
  _3 _3 (.in_1(in_1), .out_2(_3_out_2));
  _5 _5 (.in_1(in_1), .out_2(_5_out_2));
  _6 _6 (.in_1(in_1), .out_2(_6_out_2));
  _8 _8 (.in_1(in_1), .out_2(_8_out_2));
  _9 _9 (.in_1(in_1), .out_2(_9_out_2));
  _11 _11 (.in_1(in_1), .out_2(_11_out_2));
  _12 _12 (.in_1(in_1), .out_2(_12_out_2));
  _13 _13 (.in_1(in_1), .out_2(_13_out_2));
  _14 _14 (.in_1(in_1), .out_2(_14_out_2));
  _0 _0 (.in_1(in_1), .out_2(_0_out_2));
  or D (out_2, _2_out_2, _3_out_2, _5_out_2, _6_out_2, _8_out_2, _9_out_2, _11_out_2, _12_out_2, _13_out_2, _14_out_2, _0_out_2);
endmodule

module E (
  input  [3:0] in_1,
  output out_2
);

  wire _0_out_2, _2_out_2, _6_out_2, _8_out_2, _10_out_2, _11_out_2, _12_out_2, _13_out_2, _14_out_2,
       _15_out_2;

  _2 _2 (.in_1(in_1), .out_2(_2_out_2));
  _6 _6 (.in_1(in_1), .out_2(_6_out_2));
  _8 _8 (.in_1(in_1), .out_2(_8_out_2));
  _10 _10 (.in_1(in_1), .out_2(_10_out_2));
  _11 _11 (.in_1(in_1), .out_2(_11_out_2));
  _12 _12 (.in_1(in_1), .out_2(_12_out_2));
  _13 _13 (.in_1(in_1), .out_2(_13_out_2));
  _14 _14 (.in_1(in_1), .out_2(_14_out_2));
  _15 _15 (.in_1(in_1), .out_2(_15_out_2));
  _0 _0 (.in_1(in_1), .out_2(_0_out_2));
  or E (out_2, _2_out_2, _6_out_2, _8_out_2, _0_out_2, _10_out_2, _11_out_2, _12_out_2, _13_out_2, _14_out_2, _15_out_2);
endmodule

module F (
  input  [3:0] in_1,
  output out_2
);

  wire _0_out_2, _4_out_2, _5_out_2, _6_out_2, _8_out_2, _9_out_2, _10_out_2, _11_out_2, _12_out_2,
       _14_out_2, _15_out_2;

  _4 _4 (.in_1(in_1), .out_2(_4_out_2));
  _5 _5 (.in_1(in_1), .out_2(_5_out_2));
  _6 _6 (.in_1(in_1), .out_2(_6_out_2));
  _8 _8 (.in_1(in_1), .out_2(_8_out_2));
  _9 _9 (.in_1(in_1), .out_2(_9_out_2));
  _10 _10 (.in_1(in_1), .out_2(_10_out_2));
  _11 _11 (.in_1(in_1), .out_2(_11_out_2));
  _12 _12 (.in_1(in_1), .out_2(_12_out_2));
  _14 _14 (.in_1(in_1), .out_2(_14_out_2));
  _15 _15 (.in_1(in_1), .out_2(_15_out_2));
  _0 _0 (.in_1(in_1), .out_2(_0_out_2));
  or F (out_2, _4_out_2, _5_out_2, _6_out_2, _8_out_2, _9_out_2, _10_out_2, _11_out_2, _12_out_2, _0_out_2, _14_out_2, _15_out_2);
endmodule

module G (
  input  [3:0] in_1,
  output out_2
);

  wire _2_out_2, _3_out_2, _4_out_2, _5_out_2, _6_out_2, _8_out_2, _9_out_2, _10_out_2, _11_out_2, _13_out_2,
       _14_out_2, _15_out_2;

  _2 _2 (.in_1(in_1), .out_2(_2_out_2));
  _3 _3 (.in_1(in_1), .out_2(_3_out_2));
  _4 _4 (.in_1(in_1), .out_2(_4_out_2));
  _5 _5 (.in_1(in_1), .out_2(_5_out_2));
  _6 _6 (.in_1(in_1), .out_2(_6_out_2));
  _8 _8 (.in_1(in_1), .out_2(_8_out_2));
  _9 _9 (.in_1(in_1), .out_2(_9_out_2));
  _10 _10 (.in_1(in_1), .out_2(_10_out_2));
  _11 _11 (.in_1(in_1), .out_2(_11_out_2));
  _13 _13 (.in_1(in_1), .out_2(_13_out_2));
  _14 _14 (.in_1(in_1), .out_2(_14_out_2));
  _15 _15 (.in_1(in_1), .out_2(_15_out_2));
  or G (out_2, _2_out_2, _3_out_2, _4_out_2, _5_out_2, _6_out_2, _8_out_2, _9_out_2, _10_out_2, _11_out_2, _13_out_2, _14_out_2, _15_out_2);
endmodule

module _0 (
  input  [3:0] in_1,
  output out_2
);

  wire not_1_out, not_2_out, not_3_out, not_4_out;

  not not_1 (not_1_out, in_1[3]);
  not not_2 (not_2_out, in_1[2]);
  not not_3 (not_3_out, in_1[1]);
  not not_4 (not_4_out, in_1[0]);
  and and_1 (out_2, not_1_out, not_2_out, not_3_out, not_4_out);
endmodule

module add_afficheur (
  input  [3:0] bin1,
  input  [3:0] bin2
);

  wire [3:0] bin1_bin2_out_3;
  wire [7:0] afficheur7segments_1_out_2, afficheur7segments_2_out_2, bin3_out_2;

  add4bits bin1_bin2 (.in_1(bin1), .in_2(bin2), .out_3(bin1_bin2_out_3));
  AFFICHEUR7SEGMENTS afficheur7segments_1 (.bin(bin1), .out_2(afficheur7segments_1_out_2));
  AFFICHEUR7SEGMENTS afficheur7segments_2 (.bin(bin2), .out_2(afficheur7segments_2_out_2));
  AFFICHEUR7SEGMENTS bin3 (.bin(bin1_bin2_out_3), .out_2(bin3_out_2));
  _7_Segment_Display u_7_segment_display_1 (
    .g(afficheur7segments_1_out_2[0]), .f(afficheur7segments_1_out_2[1]), .a(afficheur7segments_1_out_2[2]),
    .b(afficheur7segments_1_out_2[3]), .e(afficheur7segments_1_out_2[4]), .d(afficheur7segments_1_out_2[5]),
    .c(afficheur7segments_1_out_2[6]), .dp(afficheur7segments_1_out_2[7]));
  _7_Segment_Display u_7_segment_display_2 (
    .g(afficheur7segments_2_out_2[0]), .f(afficheur7segments_2_out_2[1]), .a(afficheur7segments_2_out_2[2]),
    .b(afficheur7segments_2_out_2[3]), .e(afficheur7segments_2_out_2[4]), .d(afficheur7segments_2_out_2[5]),
    .c(afficheur7segments_2_out_2[6]), .dp(afficheur7segments_2_out_2[7]));
  _7_Segment_Display u_7_segment_display_3 (
    .g(bin3_out_2[0]), .f(bin3_out_2[1]), .a(bin3_out_2[2]), .b(bin3_out_2[3]), .e(bin3_out_2[4]),
    .d(bin3_out_2[5]), .c(bin3_out_2[6]), .dp(bin3_out_2[7]));
endmodule

module add4bits (
  input  [3:0] in_1,
  input  [3:0] in_2,
  output [3:0] out_3
);

  wire adder_1_cout, adder_2_cout, adder_3_cout;

  Adder #(.width(1)) adder_1 (.a(in_1[0]), .b(in_2[0]), .out(out_3[0]), .cin(1'b0), .cout(adder_1_cout));
  Adder #(.width(1)) adder_2 (.a(in_1[1]), .b(in_2[1]), .out(out_3[1]), .cin(adder_1_cout), .cout(adder_2_cout));
  Adder #(.width(1)) adder_3 (.a(in_1[2]), .b(in_2[2]), .out(out_3[2]), .cin(adder_2_cout), .cout(adder_3_cout));
  Adder #(.width(1)) adder_4 (.a(in_1[3]), .b(in_2[3]), .out(out_3[3]), .cin(adder_3_cout));  // open: cout
endmodule
